# Fritzing sketch blink-button (saved by Fritzing 0.8.7b)
breadboards: 1

parts:
  Raspberry_Pi_B_rev1 = Raspberry Pi B rev2
  R1 = Resistor [tolerance=±5% resistance=220 package=THT]
  LED1 = LED - 5mm [color="Red (633nm)" package="5 mm [THT]"]
  S1 = Pushbutton [package="[THT]"]
  R2 = Resistor [tolerance=±5% resistance=100k package=THT]

nets:
  N1: Raspberry_Pi_B_rev1.3V3, S1.Pin_1, S1.Pin_2
  N2: Raspberry_Pi_B_rev1.GND, R1.Pin_0, R2.Pin_0
  N3: Raspberry_Pi_B_rev1.GPIO_23, S1.Pin_3, S1.Pin_4, R2.Pin_1
  N4: Raspberry_Pi_B_rev1.GPIO_18, LED1.cathode
  N5: R1.Pin_1, LED1.anode
